// Logisim project d latch.circ as structural Verilog: 2 circuits, main circuit d-latch
module d_latch (
  input  in_1,
  input  in_2,
  output Q,
  output Q_prime
);

  wire and_1_out, and_2_out, nor_1_out, nor_2_out, not_1_out;

  not not_1 (not_1_out, in_2);
  and and_1 (and_1_out, not_1_out, in_1);
  and and_2 (and_2_out, in_1, in_2);
  nor nor_1 (nor_1_out, and_1_out, nor_2_out);
  nor nor_2 (nor_2_out, nor_1_out, and_2_out);
endmodule

module d_flip_flop (
  input  d,
  output q,
  output q_prime
);

  wire clock_1_out, d_latch_1_p2, d_latch_1_p3, not_2_out;

  Clock clock_1 (.out(clock_1_out));
  // d_latch d_latch_1: pin names not known; wires that end beside it: d, d_latch_1_p2, d_latch_1_p3
  not not_1 (d_latch_1_p2, clock_1_out);
  not not_2 (not_2_out, d_latch_1_p2);
  // d_latch d_latch_2: pin names not known; wires that end beside it: d_latch_1_p3, not_2_out, q, q_prime
endmodule
